# Fritzing sketch WiringDiagram (saved by Fritzing 1.0.1rc)
circuit board: 18cm x 5cm

parts:
  Pixel_L_1 = Adafruit Breadboard-Friendly NeoPixel [part_number="Adafruit #4356"]
  Pixel_L_2 = Adafruit Breadboard-Friendly NeoPixel [part_number="Adafruit #4356"]
  Pixel_L_3 = Adafruit Breadboard-Friendly NeoPixel [part_number="Adafruit #4356"]
  Pixel_L_4 = Adafruit Breadboard-Friendly NeoPixel [part_number="Adafruit #4356"]
  Pixel_L_5 = Adafruit Breadboard-Friendly NeoPixel [part_number="Adafruit #4356"]
  Pixel_L_6 = Adafruit Breadboard-Friendly NeoPixel [part_number="Adafruit #1312"]
  Pixel_L_7 = Adafruit Breadboard-Friendly NeoPixel [part_number="Adafruit #4356"]
  Pixel_R_1 = Adafruit Breadboard-Friendly NeoPixel [part_number="Adafruit #4356"]
  Pixel_R_2 = Adafruit Breadboard-Friendly NeoPixel [part_number="Adafruit #4356"]
  Pixel_R_3 = Adafruit Breadboard-Friendly NeoPixel [part_number="Adafruit #4356"]
  Pixel_R_4 = Adafruit Breadboard-Friendly NeoPixel [part_number="Adafruit #4356"]
  Pixel_R_5 = Adafruit Breadboard-Friendly NeoPixel [part_number="Adafruit #4356"]
  Pixel_R_6 = Adafruit Breadboard-Friendly NeoPixel [part_number="Adafruit #4356"]
  Pixel_R_7 = Adafruit Breadboard-Friendly NeoPixel [part_number="Adafruit #4356"]
  S1 = SWITCH-DPDT [package=os]
  TouchSensor = Adafruit Standalone 5-Pad Capacitive Touch Sensor Breakout - AT42QT1070 [part_number="Adafruit #1362"]
  Adafruit_Feather_RP2040_SCORPIO1 = Adafruit Feather RP2040 SCORPIO [part_number=#5650]

nets:
  N1: Pixel_L_1.IN, Adafruit_Feather_RP2040_SCORPIO1.NEO0
  GND: Pixel_L_1.GND, Pixel_L_2.GND, Pixel_L_3.GND, Pixel_L_4.GND, Pixel_L_5.GND, Pixel_L_6.GND, Pixel_L_7.GND, Pixel_R_1.GND, Pixel_R_2.GND, Pixel_R_3.GND, Pixel_R_4.GND, Pixel_R_5.GND, Pixel_R_6.GND, Pixel_R_7.GND, S1.5, TouchSensor.GND, Adafruit_Feather_RP2040_SCORPIO1.GND
  VDD: Pixel_L_1.VDD, Pixel_L_2.VDD, Pixel_L_3.VDD, Pixel_L_4.VDD, Pixel_L_5.VDD, Pixel_L_6.VDD, Pixel_L_7.VDD, Pixel_R_1.VDD, Pixel_R_2.VDD, Pixel_R_3.VDD, Pixel_R_4.VDD, Pixel_R_5.VDD, Pixel_R_6.VDD, Pixel_R_7.VDD, S1.3
  N2: Pixel_L_1.OUT, Pixel_L_2.IN
  N3: Pixel_L_2.OUT, Pixel_L_3.IN
  N4: Pixel_L_3.OUT, Pixel_L_4.IN
  N5: Pixel_L_4.OUT, Pixel_L_5.IN
  N6: Pixel_L_5.OUT, Pixel_L_6.IN
  N7: Pixel_L_6.OUT, Pixel_L_7.IN
  N8: Pixel_R_1.IN, Adafruit_Feather_RP2040_SCORPIO1.NEO1
  N9: Pixel_R_1.OUT, Pixel_R_2.IN
  N10: Pixel_R_2.OUT, Pixel_R_3.IN
  N11: Pixel_R_3.OUT, Pixel_R_4.IN
  N12: Pixel_R_4.OUT, Pixel_R_5.IN
  N13: Pixel_R_5.OUT, Pixel_R_6.IN
  N14: Pixel_R_6.OUT, Pixel_R_7.IN
  N15: S1.2, Adafruit_Feather_RP2040_SCORPIO1.VBAT
  N16: S1.6, Adafruit_Feather_RP2040_SCORPIO1.EN
  N17: TouchSensor.VDD, Adafruit_Feather_RP2040_SCORPIO1.D6
  N18: TouchSensor.OUT1, Adafruit_Feather_RP2040_SCORPIO1.D5

custom parts:
  Adafruit Breadboard-Friendly NeoPixel: This is the easiest way possible to add small, bright RGB pixels to your project. We took the same technology from our Flora NeoPixels and made them breadboard friendly, with two rows of 3 x 0.1" spaced header on each side for easy soldering, chaining and breadboarding. These ultra-bright LEDs have a constant-current driver cooked right into the LED package! The pixels are chainable - so you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
  Adafruit Standalone 5-Pad Capacitive Touch Sensor Breakout - AT42QT1070: This breakout board is the simplest way to create a project with mutiple capacitive touch sensors. No microcontroller is required here - just power with 1.8 to 5.5VDC and connect up to 5 conductive pads to the 5 left-hand pins. When a capacitive load is detected (e.g. a person touches one of the conductive contacts) the corresponding LED on the right lights up and the output pin goes low. You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
  Adafruit Feather RP2040 SCORPIO: If there is one thing Adafruit is known for, its mega-blinky-fun-rainbow-LEDs. We just love sticking NeoPixels anywhere and everywhere. When we saw the new 'PIO' peripheral on the RP2040 from Raspberry Pi, we just knew it would be perfect for driving large quantities of NeoPixels. So we created this board, the Adafruit Feather RP2040 SCORPIO, designed specifically for NeoPixel (WS2812) driving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
